# Fritzing sketch MositureSensorLogic (saved by Fritzing 0.9.3b)
breadboards: 1

parts:
  ESP-12F_w/breakout = Gizwits WiFi Witty ESP-12F
  BAT1 = Battery Holders [package=battery-aa]
  LED1 = RGB LED (com. cathode, rbg) [package="5 mm [THT]"]
  S1_-_FLASH = SPST Switch [package=switch-spdt-smd]
  S2_-_RESET = SWITCH-MOMENTARY-2 [package=tactile_switch_tall]
  Part1 = Soil Moisture Sensor
  R1 = Resistor [tolerance=±5% resistance=10k package="0402 [SMD]"]
  R2_/_R3_/_R4 = Resistor [tolerance=±5% resistance=470 package="0402 [SMD]"]
  R2_/_R3_/_R5 = Resistor [tolerance=±5% resistance=470 package="0402 [SMD]"]
  R2_/_R3_/_R6 = Resistor [tolerance=±5% resistance=470 package="0402 [SMD]"]
  R2 = Resistor [tolerance=±5% resistance=10k package="0402 [SMD]"]
  R3 = Resistor [tolerance=±5% resistance=15k package="0402 [SMD]"]

nets:
  N1: ESP-12F_w/breakout.REST, ESP-12F_w/breakout.GPIO16, S2_-_RESET.1
  VCC: ESP-12F_w/breakout.CH_PD, ESP-12F_w/breakout.VCC, BAT1.+, Part1.VCC, R1.Pin_1
  N2: ESP-12F_w/breakout.GPIO14, R2_/_R3_/_R5.Pin_0
  N3: ESP-12F_w/breakout.GPIO12, R2_/_R3_/_R6.Pin_0
  N4: ESP-12F_w/breakout.GPIO13, R2_/_R3_/_R4.Pin_0
  GND: ESP-12F_w/breakout.GND, ESP-12F_w/breakout.GPIO15, BAT1.-, LED1.common_cathode, S1_-_FLASH.S, S2_-_RESET.2, Part1.GND, R2.Pin_1
  N5: ESP-12F_w/breakout.GPIO0, S1_-_FLASH.P
  N6: LED1.red_anode, R2_/_R3_/_R4.Pin_1
  N7: LED1.blue_anode, R2_/_R3_/_R5.Pin_1
  N8: LED1.green_anode, R2_/_R3_/_R6.Pin_1
  N9: S1_-_FLASH.O, R1.Pin_0
  N10: R2.Pin_0, R3.Pin_1
